// Logisim project 3-bit cpu.circ as structural Verilog
module SHR (
  input  [2:0] A,
  input  [1:0] Shift,
  output [2:0] O
);

  Multiplexer #(.select(2), .enable("false")) multiplexer_1 (
    .in0(A[2]), .in1(1'b0), .in2(1'b0), .out(O[2]), .sel(Shift));  // open: in3
  Multiplexer #(.select(2), .enable("false")) multiplexer_2 (
    .in0(A[1]), .in1(A[2]), .in2(1'b0), .out(O[1]), .sel(Shift));  // open: in3
  Multiplexer #(.select(2), .enable("false")) multiplexer_3 (
    .in0(A[0]), .in1(A[1]), .in2(A[2]), .out(O[0]), .sel(Shift));  // open: in3
endmodule

module SHL (
  input  [2:0] A,
  input  [1:0] Shift,
  output [2:0] O
);

  Multiplexer #(.select(2), .enable("false")) multiplexer_1 (
    .in0(A[2]), .in1(A[1]), .in2(A[0]), .out(O[2]), .sel(Shift));  // open: in3
  Multiplexer #(.select(2), .enable("false")) multiplexer_2 (
    .in0(A[1]), .in1(A[0]), .in2(1'b0), .out(O[1]), .sel(Shift));  // open: in3
  Multiplexer #(.select(2), .enable("false")) multiplexer_3 (
    .in0(A[0]), .in1(1'b0), .in2(1'b0), .out(O[0]), .sel(Shift));  // open: in3
endmodule

module _3_bit_alu (
  input  [2:0] A__2_0,
  input  [2:0] B_2_0,
  input  Opcode,
  output CF,
  output [2:0] R
);

  wire [2:0] SHL, SHR;

  Multiplexer #(.width(3), .enable("false")) multiplexer_1 (.in0(SHR), .in1(SHL), .out(R), .sel(Opcode));
  SHL shl_1 (.A(A__2_0), .O(SHL), .Shift(B_2_0[1:0]));
  SHR shr_1 (.A(A__2_0), .Shift(B_2_0[1:0]), .O(SHR));

  assign CF = 1'b0;

  // Other names for the same wires on the sheet: A[2:0] = A__2_0; B[2:0] = B_2_0; Shift[1:0] = B_2_0[1:0]
endmodule

module alu_test (
  input  [2:0] A,
  input  [2:0] B,
  input  OP,
  output [2:0] R,
  output CF,
  output DIV_Excep,
  output MUL_Excep
);

  // _3_bit_alu 3_bit_alu_1: pin names not known; wires that end beside it: OP, DIV_Excep, A, CF, B, R, MUL_Excep
endmodule

module _1bit_register (
  input  Din,
  input  Sel,
  input  Clock,
  output Dout
);

  wire n1bit_2_to_1_mux_1_out;

  _1bit_2_to_1_MUX u_1bit_2_to_1_mux_1 (.A(Dout), .Sel(Sel), .B(Din), .Out(n1bit_2_to_1_mux_1_out));
  D_Flip_Flop d_ff_1 (.clk(Clock), .D(n1bit_2_to_1_mux_1_out), .Q(Dout));  // open: Qn, preset, en, reset
endmodule

module _1bit_2_to_1_MUX (
  input  A,
  input  Sel,
  input  B,
  output Out
);

  wire and_1_out, and_2_out, not_1_out;

  not not_1 (not_1_out, Sel);
  and and_1 (and_1_out, A, not_1_out);
  and and_2 (and_2_out, Sel, B);
  or or_1 (Out, and_1_out, and_2_out);
endmodule

module Register_set (
  input  [2:0] WRD,
  input  WE,
  input  [2:0] Wr,
  input  [2:0] RA,
  input  [2:0] RB,
  input  CLK,
  output [2:0] A,
  output [2:0] B
);

  wire decoder_1_out0, decoder_1_out1, decoder_1_out2, decoder_1_out3, decoder_1_out4;
  wire [2:0] R0, R1, R2, R3, R4;

  Decoder #(.select(3)) decoder_1 (
    .out0(decoder_1_out0), .out1(decoder_1_out1), .out2(decoder_1_out2), .out3(decoder_1_out3),
    .out4(decoder_1_out4), .sel(Wr), .en(WE));  // open: out5, out6, out7
  _3_bit_register u_3_bit_register_1 (.Din_2_0(WRD), .Sel(decoder_1_out0), .Clock(CLK), .Dout_2_0(R0));
  _3_bit_register u_3_bit_register_2 (.Din_2_0(WRD), .Sel(decoder_1_out1), .Clock(CLK), .Dout_2_0(R1));
  _3_bit_register u_3_bit_register_3 (.Din_2_0(WRD), .Sel(decoder_1_out2), .Clock(CLK), .Dout_2_0(R2));
  _3_bit_register u_3_bit_register_4 (.Din_2_0(WRD), .Sel(decoder_1_out3), .Clock(CLK), .Dout_2_0(R3));
  _3_bit_register u_3_bit_register_5 (.Din_2_0(WRD), .Sel(decoder_1_out4), .Clock(CLK), .Dout_2_0(R4));
  Multiplexer #(.select(3), .width(3), .enable("false")) multiplexer_1 (
    .in0(R0), .in1(R1), .in2(R2), .in3(R3), .in4(R4), .out(A), .sel(RA));  // open: in5, in6, in7
  Multiplexer #(.select(3), .width(3), .enable("false")) multiplexer_2 (
    .in0(R0), .in1(R1), .in2(R2), .in3(R3), .in4(R4), .out(B), .sel(RB));  // open: in5, in6, in7
endmodule

module _3_bit_register (
  input  [2:0] Din_2_0,
  input  Sel,
  input  Clock,
  output [2:0] Dout_2_0
);

  _1bit_register u_1bit_register_1 (.Din(Din_2_0[0]), .Sel(Sel), .Clock(Clock), .Dout(Dout_2_0[0]));
  _1bit_register u_1bit_register_2 (.Din(Din_2_0[1]), .Sel(Sel), .Clock(Clock), .Dout(Dout_2_0[1]));
  _1bit_register u_1bit_register_3 (.Din(Din_2_0[2]), .Sel(Sel), .Clock(Clock), .Dout(Dout_2_0[2]));
endmodule

module _1x1SRAM (
  input  Read_Select1,
  input  Read_Select2,
  input  Write_Data,
  input  Write_Select,
  input  Clock,
  output Read_Data1,
  output Read_Data2
);

  wire d_ff_1_q, multiplexer_1_out;

  Multiplexer #(.enable("false")) multiplexer_1 (
    .in0(d_ff_1_q), .in1(Write_Data), .out(multiplexer_1_out), .sel(Write_Select));
  D_Flip_Flop d_ff_1 (.clk(Clock), .D(multiplexer_1_out), .Q(d_ff_1_q));  // open: Qn, preset, en, reset
  and and_1 (Read_Data1, Read_Select1, d_ff_1_q);
  and and_2 (Read_Data2, Read_Select2, d_ff_1_q);
endmodule

module Flag_Register (
  input  CF,
  input  SF,
  input  ZF,
  input  Clock,
  output CF_2,
  output SF_2,
  output ZF_2
);

  _1bit_register u_1bit_register_1 (.Din(CF), .Sel(1'b1), .Clock(Clock), .Dout(CF_2));
  _1bit_register u_1bit_register_2 (.Din(SF), .Sel(1'b1), .Clock(Clock), .Dout(SF_2));
  _1bit_register u_1bit_register_3 (.Din(ZF), .Sel(1'b1), .Clock(Clock), .Dout(ZF_2));
endmodule

module _1x16SRAM (
  input  CLK,
  input  Write_Select,
  input  Read_Select1,
  input  Read_Select2,
  input  [15:0] Write_Data_15_0,
  output [15:0] Read_Data1,
  output [15:0] Read_Data2
);

  _1x1SRAM u_1x1sram_1 (
    .Read_Select1(Read_Select1), .Read_Select2(Read_Select2), .Write_Data(Write_Data_15_0[0]),
    .Write_Select(Write_Select), .Clock(CLK), .Read_Data1(Read_Data1[0]), .Read_Data2(Read_Data2[0]));
  _1x1SRAM u_1x1sram_2 (
    .Read_Select1(Read_Select1), .Read_Select2(Read_Select2), .Write_Data(Write_Data_15_0[4]),
    .Write_Select(Write_Select), .Clock(CLK), .Read_Data1(Read_Data1[4]), .Read_Data2(Read_Data2[4]));
  _1x1SRAM u_1x1sram_3 (
    .Read_Select1(Read_Select1), .Read_Select2(Read_Select2), .Write_Data(Write_Data_15_0[8]),
    .Write_Select(Write_Select), .Clock(CLK), .Read_Data1(Read_Data1[8]), .Read_Data2(Read_Data2[8]));
  _1x1SRAM u_1x1sram_4 (
    .Read_Select1(Read_Select1), .Read_Select2(Read_Select2), .Write_Data(Write_Data_15_0[12]),
    .Write_Select(Write_Select), .Clock(CLK), .Read_Data1(Read_Data1[12]), .Read_Data2(Read_Data2[12]));
  _1x1SRAM u_1x1sram_5 (
    .Read_Select1(Read_Select1), .Read_Select2(Read_Select2), .Write_Data(Write_Data_15_0[1]),
    .Write_Select(Write_Select), .Clock(CLK), .Read_Data1(Read_Data1[1]), .Read_Data2(Read_Data2[1]));
  _1x1SRAM u_1x1sram_6 (
    .Read_Select1(Read_Select1), .Read_Select2(Read_Select2), .Write_Data(Write_Data_15_0[5]),
    .Write_Select(Write_Select), .Clock(CLK), .Read_Data1(Read_Data1[5]), .Read_Data2(Read_Data2[5]));
  _1x1SRAM u_1x1sram_7 (
    .Read_Select1(Read_Select1), .Read_Select2(Read_Select2), .Write_Data(Write_Data_15_0[9]),
    .Write_Select(Write_Select), .Clock(CLK), .Read_Data1(Read_Data1[9]), .Read_Data2(Read_Data2[9]));
  _1x1SRAM u_1x1sram_8 (
    .Read_Select1(Read_Select1), .Read_Select2(Read_Select2), .Write_Data(Write_Data_15_0[13]),
    .Write_Select(Write_Select), .Clock(CLK), .Read_Data1(Read_Data1[13]), .Read_Data2(Read_Data2[13]));
  _1x1SRAM u_1x1sram_9 (
    .Read_Select1(Read_Select1), .Read_Select2(Read_Select2), .Write_Data(Write_Data_15_0[2]),
    .Write_Select(Write_Select), .Clock(CLK), .Read_Data1(Read_Data1[2]), .Read_Data2(Read_Data2[2]));
  _1x1SRAM u_1x1sram_10 (
    .Read_Select1(Read_Select1), .Read_Select2(Read_Select2), .Write_Data(Write_Data_15_0[6]),
    .Write_Select(Write_Select), .Clock(CLK), .Read_Data1(Read_Data1[6]), .Read_Data2(Read_Data2[6]));
  _1x1SRAM u_1x1sram_11 (
    .Read_Select1(Read_Select1), .Read_Select2(Read_Select2), .Write_Data(Write_Data_15_0[10]),
    .Write_Select(Write_Select), .Clock(CLK), .Read_Data1(Read_Data1[10]), .Read_Data2(Read_Data2[10]));
  _1x1SRAM u_1x1sram_12 (
    .Read_Select1(Read_Select1), .Read_Select2(Read_Select2), .Write_Data(Write_Data_15_0[14]),
    .Write_Select(Write_Select), .Clock(CLK), .Read_Data1(Read_Data1[14]), .Read_Data2(Read_Data2[14]));
  _1x1SRAM u_1x1sram_13 (
    .Read_Select1(Read_Select1), .Read_Select2(Read_Select2), .Write_Data(Write_Data_15_0[3]),
    .Write_Select(Write_Select), .Clock(CLK), .Read_Data1(Read_Data1[3]), .Read_Data2(Read_Data2[3]));
  _1x1SRAM u_1x1sram_14 (
    .Read_Select1(Read_Select1), .Read_Select2(Read_Select2), .Write_Data(Write_Data_15_0[7]),
    .Write_Select(Write_Select), .Clock(CLK), .Read_Data1(Read_Data1[7]), .Read_Data2(Read_Data2[7]));
  _1x1SRAM u_1x1sram_15 (
    .Read_Select1(Read_Select1), .Read_Select2(Read_Select2), .Write_Data(Write_Data_15_0[11]),
    .Write_Select(Write_Select), .Clock(CLK), .Read_Data1(Read_Data1[11]), .Read_Data2(Read_Data2[11]));
  _1x1SRAM u_1x1sram_16 (
    .Read_Select1(Read_Select1), .Read_Select2(Read_Select2), .Write_Data(Write_Data_15_0[15]),
    .Write_Select(Write_Select), .Clock(CLK), .Read_Data1(Read_Data1[15]), .Read_Data2(Read_Data2[15]));

  // Other names for the same wires on the sheet: RD1_0 = Read_Data1[0]; RD1_1 = Read_Data1[1]; RD1_2 = Read_Data1[2];
  //   RD1_3 = Read_Data1[3]; RD1_4 = Read_Data1[4]; RD1_5 = Read_Data1[5]; RD1_6 = Read_Data1[6];
  //   RD1_7 = Read_Data1[7]; RD1_8 = Read_Data1[8]; RD1_9 = Read_Data1[9]; RD1_10 = Read_Data1[10];
  //   RD1_11 = Read_Data1[11]; RD1_12 = Read_Data1[12]; RD1_13 = Read_Data1[13]; RD1_14 = Read_Data1[14];
  //   RD1_15 = Read_Data1[15]; Rd2_0 = Read_Data2[0]; Rd2_1 = Read_Data2[1]; Rd2_2 = Read_Data2[2];
  //   Rd2_3 = Read_Data2[3]; Rd2_4 = Read_Data2[4]; Rd2_5 = Read_Data2[5]; Rd2_6 = Read_Data2[6];
  //   Rd2_7 = Read_Data2[7]; Rd2_8 = Read_Data2[8]; Rd2_9 = Read_Data2[9]; Rd2_10 = Read_Data2[10];
  //   Rd2_11 = Read_Data2[11]; Rd2_12 = Read_Data2[12]; Rd2_13 = Read_Data2[13]; Rd2_14 = Read_Data2[14];
  //   Rd2_15 = Read_Data2[15]; RS1 = Read_Select1; RS2 = Read_Select2; D0 = Write_Data_15_0[0];
  //   D1 = Write_Data_15_0[1]; D2 = Write_Data_15_0[2]; D3 = Write_Data_15_0[3]; D4 = Write_Data_15_0[4];
  //   D5 = Write_Data_15_0[5]; D6 = Write_Data_15_0[6]; D7 = Write_Data_15_0[7]; D8 = Write_Data_15_0[8];
  //   D9 = Write_Data_15_0[9]; D10 = Write_Data_15_0[10]; D11 = Write_Data_15_0[11]; D12 = Write_Data_15_0[12];
  //   D13 = Write_Data_15_0[13]; D14 = Write_Data_15_0[14]; D15 = Write_Data_15_0[15]; WS = Write_Select
endmodule

module _8x16SRAM (
  input  [15:0] Write_Data_15_0,
  input  [2:0] Read_Address1_2_0,
  input  [2:0] Read_Address2_2_0,
  input  WE,
  input  [2:0] Write_Address_2_0,
  input  CLK,
  output [15:0] Read_Data1_15_0,
  output [15:0] Read_Data2_15_0
);

  wire R1_0, R1_1, R1_2, R1_3, R1_4, R1_5, R1_6, R1_7, R2_0, R2_1, R2_2, R2_3, R2_4, R2_5, R2_6, R2_7, W0,
       W1, W2, W3, W4, W5, W6, W7;
  wire [15:0] RD1_0, RD1_1, RD1_2, RD1_3, RD1_4, RD1_5, RD1_6, RD1_7, RD2_0, RD2_1, RD2_2, RD2_3, RD2_4,
       RD2_5, RD2_6, RD2_7;

  Decoder #(.select(3), .enable("false")) decoder_1 (
    .out0(R1_0), .out1(R1_1), .out2(R1_2), .out3(R1_3), .out4(R1_4), .out5(R1_5), .out6(R1_6), .out7(R1_7),
    .sel(Read_Address1_2_0));
  Decoder #(.select(3), .enable("false")) decoder_2 (
    .out0(R2_0), .out1(R2_1), .out2(R2_2), .out3(R2_3), .out4(R2_4), .out5(R2_5), .out6(R2_6), .out7(R2_7),
    .sel(Read_Address2_2_0));
  Decoder #(.select(3)) decoder_3 (
    .out0(W0), .out1(W1), .out2(W2), .out3(W3), .out4(W4), .out5(W5), .out6(W6), .out7(W7),
    .sel(Write_Address_2_0), .en(WE));
  _1x16SRAM u_1x16sram_1 (
    .CLK(CLK), .Write_Select(W0), .Read_Select1(R1_0), .Read_Select2(R2_0),
    .Write_Data_15_0(Write_Data_15_0), .Read_Data1(RD1_0), .Read_Data2(RD2_0));
  _1x16SRAM u_1x16sram_2 (
    .CLK(CLK), .Write_Select(W1), .Read_Select1(R1_1), .Read_Select2(R2_1),
    .Write_Data_15_0(Write_Data_15_0), .Read_Data1(RD1_1), .Read_Data2(RD2_1));
  _1x16SRAM u_1x16sram_3 (
    .CLK(CLK), .Write_Select(W2), .Read_Select1(R1_2), .Read_Select2(R2_2),
    .Write_Data_15_0(Write_Data_15_0), .Read_Data1(RD1_2), .Read_Data2(RD2_2));
  _1x16SRAM u_1x16sram_4 (
    .CLK(CLK), .Write_Select(W3), .Read_Select1(R1_3), .Read_Select2(R2_3),
    .Write_Data_15_0(Write_Data_15_0), .Read_Data1(RD1_3), .Read_Data2(RD2_3));
  _1x16SRAM u_1x16sram_5 (
    .CLK(CLK), .Write_Select(W4), .Read_Select1(R1_4), .Read_Select2(R2_4),
    .Write_Data_15_0(Write_Data_15_0), .Read_Data1(RD1_4), .Read_Data2(RD2_4));
  _1x16SRAM u_1x16sram_6 (
    .CLK(CLK), .Write_Select(W5), .Read_Select1(R1_5), .Read_Select2(R2_5),
    .Write_Data_15_0(Write_Data_15_0), .Read_Data1(RD1_5), .Read_Data2(RD2_5));
  _1x16SRAM u_1x16sram_7 (
    .CLK(CLK), .Write_Select(W6), .Read_Select1(R1_6), .Read_Select2(R2_6),
    .Write_Data_15_0(Write_Data_15_0), .Read_Data1(RD1_6), .Read_Data2(RD2_6));
  _1x16SRAM u_1x16sram_8 (
    .CLK(CLK), .Write_Select(W7), .Read_Select1(R1_7), .Read_Select2(R2_7),
    .Write_Data_15_0(Write_Data_15_0), .Read_Data1(RD1_7), .Read_Data2(RD2_7));
  assign Read_Data1_15_0 = RD1_0 | RD1_1 | RD1_2 | RD1_3 | RD1_4 | RD1_5 | RD1_6 | RD1_7;  // OR_Gate or_1, 16 bits wide
  assign Read_Data2_15_0 = RD2_0 | RD2_1 | RD2_2 | RD2_3 | RD2_4 | RD2_5 | RD2_6 | RD2_7;  // OR_Gate or_2, 16 bits wide
endmodule

module _3bit_counter_register (
  input  [2:0] Din_2_0,
  input  Clock,
  output [2:0] Dout_2_0
);

  _1bit_register u_1bit_register_1 (.Din(Din_2_0[0]), .Sel(1'b1), .Clock(Clock), .Dout(Dout_2_0[0]));
  _1bit_register u_1bit_register_2 (.Din(Din_2_0[1]), .Sel(1'b1), .Clock(Clock), .Dout(Dout_2_0[1]));
  _1bit_register u_1bit_register_3 (.Din(Din_2_0[2]), .Sel(1'b1), .Clock(Clock), .Dout(Dout_2_0[2]));
endmodule

module _3bit_PC_Adder (
  input  [2:0] I_2_0,
  output [2:0] O_2_0
);

  wire [2:0] bit_extender_1_out;

  assign bit_extender_1_out = {{2{1'b0}}, 1'b1};  // Bit_Extender bit_extender_1
  Adder #(.width(3)) adder_1 (.a(I_2_0), .b(bit_extender_1_out), .out(O_2_0));  // open: cin, cout
endmodule

module Control_Unit (
  input  [2:0] Opcode_2_0,
  output Op,
  output Imm_Sel,
  output WE,
  output JMP_Sel
);

  wire and_2_out, and_3_out, and_4_out, not_1_out, not_2_out, not_3_out, not_4_out, not_5_out, not_6_out;

  not not_1 (not_1_out, Opcode_2_0[2]);
  not not_2 (not_2_out, Opcode_2_0[2]);
  not not_3 (not_3_out, Opcode_2_0[1]);
  and and_1 (Imm_Sel, not_1_out, Opcode_2_0[1]);
  and and_2 (and_2_out, not_2_out, not_3_out);
  and and_3 (and_3_out, Opcode_2_0[2], not_4_out);
  not not_4 (not_4_out, Opcode_2_0[1]);
  not not_5 (not_5_out, Opcode_2_0[0]);
  and and_4 (and_4_out, not_5_out, not_6_out);
  not not_6 (not_6_out, Opcode_2_0[0]);
  and and_5 (JMP_Sel, and_3_out, and_4_out);
  or or_1 (WE, Imm_Sel, and_2_out);

  assign Op = Opcode_2_0[0];
endmodule

module CPU (
  input  [2:0] Write_Address_2_0,
  input  [15:0] Write_Data_15_0,
  input  WE,
  input  Clock,
  input  Clock_EN
);

  wire CPU_CLK, Imm_Sel, JMP_Sel, n3_bit_alu_1_cf, Op, WE_t;
  wire [2:0] JMP_Addr, multiplexer_1_out, multiplexer_2_out, n3_bit_alu_1_r,
       n3bit_counter_register_1_dout_2_0, n3bit_pc_adder_1_o_2_0, register_set_1_a, register_set_1_b;
  wire [15:0] n8x16sram_1_read_data1_15_0;

  Multiplexer #(.width(3), .enable("false")) multiplexer_1 (
    .in0(n3bit_pc_adder_1_o_2_0), .in1(JMP_Addr), .out(multiplexer_1_out), .sel(JMP_Sel));
  _3bit_PC_Adder u_3bit_pc_adder_1 (.I_2_0(n3bit_counter_register_1_dout_2_0), .O_2_0(n3bit_pc_adder_1_o_2_0));
  _3bit_counter_register u_3bit_counter_register_1 (
    .Din_2_0(multiplexer_1_out), .Clock(CPU_CLK), .Dout_2_0(n3bit_counter_register_1_dout_2_0));
  and and_1 (CPU_CLK, Clock, Clock_EN);
  _8x16SRAM u_8x16sram_1 (
    .Write_Data_15_0(Write_Data_15_0), .Read_Address1_2_0(n3bit_counter_register_1_dout_2_0), .WE(WE),
    .Write_Address_2_0(Write_Address_2_0), .CLK(Clock),
    .Read_Data1_15_0({n8x16sram_1_read_data1_15_0[15:13], JMP_Addr, n8x16sram_1_read_data1_15_0[9:0]}));  // open: Read_Address2_2_0, Read_Data2_15_0
  _3_bit_alu u_3_bit_alu_1 (
    .A__2_0(register_set_1_a), .B_2_0(multiplexer_2_out), .Opcode(Op), .R(n3_bit_alu_1_r),
    .CF(n3_bit_alu_1_cf));
  Register_set register_set_1 (
    .WRD(n3_bit_alu_1_r), .WE(WE_t), .Wr(JMP_Addr), .RA(JMP_Addr), .RB(n8x16sram_1_read_data1_15_0[9:7]),
    .A(register_set_1_a), .B(register_set_1_b), .CLK(CPU_CLK));
  Multiplexer #(.width(3), .enable("false")) multiplexer_2 (
    .in0(n8x16sram_1_read_data1_15_0[9:7]), .in1(register_set_1_b), .out(multiplexer_2_out), .sel(Imm_Sel));
  Flag_Register flag_register_1 (.CF(n3_bit_alu_1_cf), .Clock(Clock));  // open: SF, ZF, CF_2, SF_2, ZF_2
  Control_Unit control_unit_1 (
    .Opcode_2_0(n8x16sram_1_read_data1_15_0[15:13]), .Op(Op), .Imm_Sel(Imm_Sel), .WE(WE_t), .JMP_Sel(JMP_Sel));

  // Other names for the same wires on the sheet: Clk = Clock

  // Notes on the sheet:
  //   Register Mode SHR=0001000110000000
  //   Immediate Mode SHR=0101000110000000
  //   Branching Mode(JNC)=1001100000000000
  //   Branching Mode:Opcode(2bit+1bit)+Address(3bit)+Unused(10bit)--> Opcode 1st 2bit = 10 + Opcode last 1bit = JNC(0)
  //   Register Mode:Opcode(2bit+1bit)+Register RA(3bit)+Register RB(3bit)+Unused(7bit) --> Opcode 1st 2bit = 00+Opcode last 1bit = SHR(0),SHL(1)
  //   Register Mode SHL=0011000110000000
  //   Immediate Mode:Opcode(2bit+1bit)+Register RA(3bit)+Immediate value(3bit)+Unused(7bit)--> Opcode 1st 2bit = 01 + Opcode last 1bit = SHR(0),SHL(1)
  //   Immediate Mode SHL=0111000110000000
endmodule
